# Fritzing sketch schema (saved by Fritzing 0.9.4)
breadboards: 1

parts:
  Componente2 = FC-28 Soil Hygrometer Module
  Componente1 = FC-28 Soil Hygrometer Module - Probe
  U2 = ESP8266 NodeMCU LoLin module

nets:
  N1: Componente2.AO, U2.A0
  N2: Componente2.POS, Componente1.POS
  N3: Componente2.NEG, Componente1.NEG

custom parts:
  FC-28 Soil Hygrometer Module: The FC-28 is a soil hygrometer module that uses the Texas Instruments LM393 comparator chip to provide an analog measurement of soil humidity. The digital output is high when soil moisture is over a certain threshold, as determined by adjusting the potentiometer.
  FC-28 Soil Hygrometer Module - Probe: The FC-28 is a soil hygrometer module that uses the Texas Instruments LM393 comparator chip to provide an analog measurement of soil humidity.
  ESP8266 NodeMCU LoLin module: ESP8266 based NodeMCU
